# Fritzing sketch Untitled Sketch (saved by Fritzing 0.9.6b)
breadboards: 1

parts:
  Componente1 = Arduino Uno (Rev3) - ICSP
  LED1 = smd LED [color="Green (560nm)" package="0805 [SMD]"]  # not connected
  LED2 = smd LED [color="Red (633nm)" package="0805 [SMD]"]  # not connected
  HC-SR04_Sensor_1 = HC-SR04 Ultrasonic Distance Sensor  # not connected
  RHT1 = Humidity and Temperature Sensor RHT03  # not connected
  LCD1 = LCD screen
  R3 = Resistor [tolerance=±5% resistance=220 package="0805 [SMD]"]  # not connected

nets:
  N1: Componente1.D8, LCD1.RS
  N2: Componente1.D9_PWM, LCD1.DB4
  N3: Componente1.D10_PWM/SS, LCD1.DB5
  N4: Componente1.D11_PWM/MOSI, LCD1.DB6
  N5: Componente1.D12/MISO, LCD1.DB7
  N6: Componente1.D7, LCD1.VDD
  N7: LCD1.V0, LCD1.LED-
