# Fritzing sketch Untitled Sketch 4 (saved by Fritzing 0.9.6b)
breadboards: 1

parts:
  Parte1 = Arduino Uno (Rev3)
  LCD1 = LCD screen
  R1 = Rotary Potentiometer (Small) [maximum_resistance=100kΩ package=THT]
  Componente1 = Thumb Joystick
  RHT1 = Humidity and Temperature Sensor RHT03
  LED1 = LED - 5mm [color="Green (570nm)" current=0.030 package="5 mm [THT]"]
  S1 = Momentary Switch [package=ksa_sealed_tac_switch]
  R2 = Resistor [tolerance=±5% power=0.25 resistance=220 package=THT]
  LED3 = LED - 5mm [color="Blue (525nm)" current=0.030 package="5 mm [THT]"]
  R3 = Resistor [tolerance=±5% power=0.25 resistance=220 package=THT]
  R4 = Resistor [tolerance=±5% power=0.25 resistance=220 package=THT]
  HC-SR04_Sensor_1 = HC-SR04 Ultrasonic Distance Sensor

nets:
  N1: Parte1.A0, Componente1.HORZ
  N2: Parte1.A1, Componente1.SEL
  N3: Parte1.A3, R3.Pin_1
  N4: Parte1.D8, HC-SR04_Sensor_1.TRIG
  N5: Parte1.D9_PWM, R2.Pin_0
  N6: Parte1.D10_PWM/SS, Componente1.VERT
  N7: Parte1.D11_PWM/MOSI, LCD1.E
  N8: Parte1.D12/MISO, LCD1.RS
  N9: Parte1.D13/SCK, S1.1, R4.Pin_0
  N10: Parte1.D2, RHT1.Data-signal
  N11: Parte1.D3_PWM, LCD1.DB7
  N12: Parte1.D4, LCD1.DB6
  N13: Parte1.D5_PWM, LCD1.DB5
  N14: Parte1.D6_PWM, LCD1.DB4
  N15: Parte1.D7, HC-SR04_Sensor_1.ECHO
  VCC: Parte1.5V, LCD1.VDD, LCD1.LED+, R1.leg1, Componente1.VCC, RHT1.GND_1, R3.Pin_0, R4.Pin_1, HC-SR04_Sensor_1.VCC
  GND: Parte1.GND, LCD1.VSS, LCD1.R/W, LCD1.LED-, R1.leg2, Componente1.GND, RHT1.GND_2, LED1.cathode, S1.3, LED3.cathode, HC-SR04_Sensor_1.GND
  N16: LCD1.V0, R1.wiper
  N17: LED1.anode, R2.Pin_1
